# Fritzing sketch vogon-veggie-sensor (saved by Fritzing 1.0.3b)
circuit board: 8.46667cm x 5.64444cm
breadboards: 1

parts:
  M1 = DOIT Esp32 DevKit v1 (30 pins long, 11 pins width) [part_number=ESP32S-PIN30]
  Part1 = BME280 Breakout
  Adafruit_VCNL1 = Adafruit VCNL4040
  Part2 = Soil Moisture Sensor

nets:
  VCC: M1.3V3, Part1.3.3V, Adafruit_VCNL1.VCC, Part2.VCC
  GND: M1.GND, Part1.GND, Adafruit_VCNL1.GND, Part2.GND
  N1: M1.D18, Part1.SDI/SDA, Adafruit_VCNL1.SDA
  N2: M1.D19, Part1.SCK/SCL, Adafruit_VCNL1.SCL
  N3: M1.D34, Part2.SIG

notes:
  3V3 - Red
  GND - Blue
  D19 - SCL - Green
  D18 - SDA - Purple
  D34 - Analog - Organe

custom parts:
  DOIT Esp32 DevKit v1 (30 pins long, 11 pins width): The DOIT Esp32 DevKit v1 is one of the development board created by DOIT to evaluate the ESP-WROOM-32 module. It is based on the ESP32 microcontroller that boasts Wifi, Bluetooth, Ethernet and Low Power support all in a single chip. (vanepp) made breadboard work, adjusted pin numbering and labels and reduced size of schematic and cleaned up pcb. This chip is 30pins long (2 x15) and 11 pins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
